# Fritzing sketch IoT (saved by Fritzing 0.9.10b)

parts:
  U1 = ESP32-38PinWide [part_number=ESP32-38PinWide]
  U2 = GAS_SENSOR [package=mq-3]
  DHT1 = DHT11 Humitidy and Temperature Sensor (3 pins)

nets:
  N1: U1.3.3, DHT1.DATA
  N2: U1.GPIO34, U2.H2
  N3: U1.GPIO35, U2.H1
  GND: U1.GND, U2.A1, DHT1.GND
  N4: U1.VIN, U2.B1
  N5: U1.GPIO0, DHT1.VDD

custom parts:
  ESP32-38PinWide: Generic 38-Pin ESP32 with wide format (only access to one side of pins on a breadboard) based on Stephen Lilley's HiLetgo ESP-WROOM-32 ESP32 ESP-32S Development Board.
  DHT11 Humitidy and Temperature Sensor (3 pins): DHT11 Humidity and Temperature Sensor (3 pins) from the design created by John De Cristofaro for Adafruit Industries.
